// Digital circuit 002_adding_numbers.dig as structural Verilog
module _002_adding_numbers (
  input  [15:0] A,
  input  [15:0] B,
  output [15:0] O
);

  wire [15:0] decoder_1_a, decoder_1_b;

  decoder decoder_1 (.instruction({B, A}), .A(decoder_1_a), .B(decoder_1_b));
  // execute execute_1: pin names not known; wires that end beside it: decoder_1_a, decoder_1_b, O
endmodule
