// Digital circuit 003_adding_multiple_numbers.dig as structural Verilog
module _003_adding_multiple_numbers (
  input  [15:0] A,
  input  [15:0] B,
  input  [15:0] A_2,
  input  [15:0] B_2,
  input  [15:0] A_3,
  input  [15:0] B_3,
  input  [15:0] A_4,
  input  [15:0] B_4,
  output [15:0] out_9,
  output [15:0] out_10,
  output [15:0] out_11,
  output [15:0] out_12
);

  wire Button_out;
  wire [1:0] counter_1_out;
  wire [15:0] demultiplexer_1_out_0, demultiplexer_1_out_1, demultiplexer_1_out_2, demultiplexer_1_out_3,
       em_decoder_1_p2, em_decoder_1_p3, em_execute_1_result;
  wire [31:0] multiplexer_1_out;

  Multiplexer #(.Selector_Bits(2), .Bits(32)) multiplexer_1 (
    .sel(counter_1_out), .in_0({B, A}), .in_1({B_2, A_2}), .in_2({B_3, A_3}), .in_3({B_4, A_4}),
    .out(multiplexer_1_out));
  // em_decoder em_decoder_1: pin names not known; wires that end beside it: multiplexer_1_out, em_decoder_1_p2, em_decoder_1_p3
  Counter #(.Bits(2)) counter_1 (.en(1'b1), .C(Button_out), .clr(1'b0), .out(counter_1_out));  // open: ovf
  Button Button (.out(Button_out));
  em_execute em_execute_1 (.A(em_decoder_1_p2), .B(em_decoder_1_p3), .Result(em_execute_1_result));
  Demultiplexer #(.Bits(16), .Selector_Bits(2)) demultiplexer_1 (
    .sel(counter_1_out), .in(em_execute_1_result), .out_0(demultiplexer_1_out_0),
    .out_1(demultiplexer_1_out_1), .out_2(demultiplexer_1_out_2), .out_3(demultiplexer_1_out_3));
  Demultiplexer #(.Selector_Bits(2)) demultiplexer_2 ();  // open: sel, in, out_0, out_1, out_2, out_3
  D_FF #(.Bits(16)) d_ff_1 (.D(demultiplexer_1_out_0), .C(Button_out), .Q(out_9));  // open: nQ
  D_FF #(.Bits(16)) d_ff_2 (.D(demultiplexer_1_out_1), .C(Button_out), .Q(out_10));  // open: nQ
  D_FF #(.Bits(16)) d_ff_3 (.D(demultiplexer_1_out_2), .C(Button_out), .Q(out_11));  // open: nQ
  D_FF #(.Bits(16)) d_ff_4 (.D(demultiplexer_1_out_3), .C(Button_out), .Q(out_12));  // open: nQ

  // Notes on the sheet:
  //   A: default 33
  //   B: default 66
  //   A_2: default 10
  //   B_2: default 5
  //   A_3: default 16
  //   B_3: default 4
  //   A_4: default 9
  //   B_4: default 8
endmodule
